# Fritzing sketch stac_flex (saved by Fritzing 0.9.3b)

parts:
  Adafruit_Atmega32u1 = Adafruit Atmega32u4 Breakout Board [part_number="Atmega 32u4"]
  R3 = Basic Flex Resistor
  R4 = Basic Flex Resistor
  R5 = Basic Flex Resistor
  R6 = Resistor [tolerance=±5% resistance=220 package=THT]

nets:
  N1: Adafruit_Atmega32u1.F0, R3.pin_1
  N2: Adafruit_Atmega32u1.F1, R4.pin_1
  N3: Adafruit_Atmega32u1.F4, R5.pin_1
  N4: Adafruit_Atmega32u1.3V, R6.Pin_0
  N5: R3.Pin_2, R4.Pin_2, R5.Pin_2, R6.Pin_1
